# Fritzing sketch Sketch_LoRa (saved by Fritzing 0.9.3b)

parts:
  Arduino_Nano = Arduino Nano (Rev3.0)
  Componente1 = Adafruit RFM9x LoRa Radio [part_number="Adafruit #3072 and #3073"]

nets:
  GND: Arduino_Nano.GND, Componente1.GND
  N1: Arduino_Nano.D2, Componente1.RST
  N2: Arduino_Nano.D3, Componente1.DIO0
  N3: Arduino_Nano.D4, Componente1.CS
  N4: Arduino_Nano.D11/MOSI, Componente1.MOSI
  N5: Arduino_Nano.D12/MISO, Componente1.MISO
  3V3: Arduino_Nano.3V3, Componente1.VIN
  N6: Arduino_Nano.D13/SCK, Componente1.SCK

notes:
  Ligação
  Arduino Nano <--> RFM9X (LoRa)
  Obs1 : Os pinos D3 e D4 podem ser trocados por outros. O pino D2 pode ser substituido por D1

custom parts:
  Adafruit RFM9x LoRa Radio: Sending data over long distances is like magic, and now you can be a magician with this range of powerful and easy-to-use radio modules. Sure, sometimes you want to talk to a computer (a good time to use WiFi) or perhaps communicate with a Phone (choose Bluetooth Low Energy!) but what if you want to send data very far? Most WiFi, Bluetooth, Zigbee and other wireless chipsets use 2.4GHz, which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
